# Fritzing sketch LCD_and_speaker (saved by Fritzing 0.9.4)
breadboards: 1

parts:
  LCD1 = LCD screen
  R1 = Rotary Potentiometer (Small) [maximum_resistance=100kΩ package=THT]
  IC1 = IC, DIP package, 24 pins [chip_label=ATP3011F4-PU]
  J1 = Piezo Speaker
  U1 = LM386 [package=dip08]
  R2 = Resistor [tolerance=±5% resistance=1k package=THT]
  R3 = Resistor [tolerance=±5% resistance=1k package=THT]
  C1 = Ceramic Capacitor [capacitance=0.1µF package="100 mil [THT, multilayer]"]
  C2 = Ceramic Capacitor [capacitance=100nF package="100 mil [THT, multilayer]"]
  Part1 = Arduino Uno (Rev3)
  R4 = Resistor [tolerance=±5% resistance=1k package=THT]

nets:
  VSS: LCD1.VSS, LCD1.R/W, LCD1.LED-, R1.leg2, IC1.pin6, IC1.pin21, J1.pin1, U1.-IN, U1.V-, C2.1, Part1.GND, R4.Pin_1
  VDD: LCD1.VDD, LCD1.LED+, IC1.pin18, U1.V+, C1.0, Part1.5V
  N1: LCD1.V0, R4.Pin_0
  N2: LCD1.RS, Part1.D13/SCK
  N3: LCD1.E, Part1.D12/MISO
  N4: LCD1.DB4, Part1.D11_PWM/MOSI
  N5: LCD1.DB5, Part1.D10_PWM/SS
  N6: LCD1.DB6, Part1.D9_PWM
  N7: LCD1.DB7, Part1.D8
  N8: R1.leg1, R3.Pin_1, C1.1
  N9: IC1.pin2, Part1.D7
  N10: IC1.pin3, Part1.D6_PWM
  N11: IC1.pin5, C2.0
  N12: IC1.pin10, R3.Pin_0
  N13: J1.pin2, U1.OUT
  N14: U1.+IN, R2.Pin_1

notes:
  0.047μF
  0.1μF
  1kΩ
