# Fritzing sketch LED_4digit_7segment_display (saved by Fritzing 0.9.4)
breadboards: 1

parts:
  Part1 = Arduino Uno (Rev3)
  7_Segment1 = 7 Segment Display  # not connected
  7_Segment2 = 7 Segment Display
  7_Segment3 = 7 Segment Display
  7_Segment4 = 7 Segment Display  # not connected
  R1 = Resistor [tolerance=±5% resistance=220 package=THT]
  R2 = Resistor [tolerance=±5% resistance=220 package=THT]
  R3 = Resistor [tolerance=±5% resistance=220 package=THT]
  R5 = Resistor [tolerance=±5% resistance=220 package=THT]

nets:
  N1: Part1.D8, R3.Pin_0
  N2: Part1.D9_PWM, R2.Pin_0
  N3: Part1.D10_PWM/SS, R5.Pin_0
  N4: Part1.D11_PWM/MOSI, 7_Segment2.common_anode, R1.Pin_1
  N5: Part1.D12/MISO, 7_Segment2.Segment_B
  N6: Part1.D13/SCK, 7_Segment3.Segment_D
  N7: Part1.D2, 7_Segment2.Segment_A
  N8: Part1.D3_PWM, 7_Segment3.common_anode, R5.Pin_1
  N9: Part1.D4, 7_Segment3.Segment_E
  N10: Part1.D5_PWM, 7_Segment2.Segment_C
  N11: Part1.D6_PWM, 7_Segment2.Segment_DP
  N12: Part1.D7, R1.Pin_0
  N13: 7_Segment3.Segment_F, R3.Pin_1
  N14: 7_Segment3.Segment_G, R2.Pin_1
