# Fritzing sketch TAMIYA_cam_program_robot_by_IRreceiver (saved by Fritzing 0.9.4)
breadboards: 1

parts:
  Part1 = Arduino Nano (Rev3.0)
  MD03A1 = Dual VNH2SP30 Motor Driver [part_number=MD03A]
  M2 = DC Motor
  Part3 = IFR520 MOS module [package=THT]
  M3 = DC Motor
  VCC1 = Battery block 9V
  Part4 = Max Power IR LED Kit
  U1 = LIPO-2000mAh [package=lipo-2000]

nets:
  GND: Part1.GND, MD03A1.VIN, VCC1.-, Part4.GND, U1.-
  N1: Part1.D3, MD03A1.OUT_1A
  N2: Part1.D5, MD03A1.OUT_1B
  N3: Part1.D6, MD03A1.OUT_2A
  N4: Part1.D9, MD03A1.OUT_2B
  N5: Part1.D10, Part4.CONTROL
  5V: Part1.5V, Part4.VCC
  N6: MD03A1.GND, U1.+
  N7: M2.pin_1, Part3.VIN
  N8: M2.pin_2, Part3.GND
  N9: Part3.V+, M3.pin_1
  N10: Part3.V-, M3.pin_2

notes:
  A-1B|A-1A|VCC|GND|B-1B|B-1A
  モーターの線はArduino側のPin設定で入れ替えられるので1Aと1Bどちらに刺してもなんとかなる
