# Fritzing sketch bi_color_matrix_led_8x8_24_pins (saved by Fritzing 0.9.4)
breadboards: 2

parts:
  Disp1 = LBT2088AH [part_number=LTP-12188M-08]  # not connected
  Part1 = Arduino Uno (Rev3)
  R1 = Resistor [tolerance=±5% resistance=150 package=THT]
  R2 = Resistor [tolerance=±5% resistance=150 package=THT]
  R3 = Resistor [tolerance=±5% resistance=150 package=THT]
  R4 = Resistor [tolerance=±5% resistance=150 package=THT]
  R5 = Resistor [tolerance=±5% resistance=150 package=THT]
  R6 = Resistor [tolerance=±5% resistance=150 package=THT]
  R7 = Resistor [tolerance=±5% resistance=150 package=THT]
  R8 = Resistor [tolerance=±5% resistance=150 package=THT]

nets:
  N1: Part1.A0, R8.Pin_1
  N2: Part1.A1, R7.Pin_1
  N3: Part1.A2, R6.Pin_1
  N4: Part1.A3, R5.Pin_1
  N5: Part1.A4/SDA, R4.Pin_0
  N6: Part1.A5/SCL, R3.Pin_0
  N7: Part1.D3_PWM, R2.Pin_0
  N8: Part1.D4, R1.Pin_0

notes:
  1
  C1G C1R R1|C2G C2R R2|C3G C3R R3|C4G C4R R4
  24 23 22|21 20 19| 18 17 16 |15 14 13
