# Fritzing sketch moisture_sensor (saved by Fritzing 0.9.4)
breadboards: 1

parts:
  Part1 = Arduino Nano (Rev3.0)
  M1 = DC Motor  # not connected
  Part2 = Soil Moisture Sensor
  M2 = fc-51 [package=THT]
  Q1 = Basic FET P-Channel [package="D2Pak [SMD]"]  # not connected
  Q2 = Basic FET P-Channel [package="D2Pak [SMD]"]
  Q3 = Basic FET P-Channel [package="D2Pak [SMD]"]
  VCC1 = Battery block 9V

nets:
  N1: Part1.GND, Q3.Gate, VCC1.-
  N2: Part1.5V, Q2.source
  N3: Part2.SIG, M2.pin1
  N4: Part2.GND, M2.pin2
  N5: Part2.VCC, M2.pin3

notes:
  VCC|GND|A0|D0
